# Fritzing sketch B3_Blink (saved by Fritzing 0.9.3b)
breadboards: 1

parts:
  LED1 = LED - 5mm [color="Green (565nm)" package="5 mm [THT]"]
  R1 = Resistor [tolerance=±1% resistance=220 package=THT]
  Part1 = Arduino Mega 2560 (Rev3)

nets:
  N1: LED1.cathode, R1.Pin_0
  N2: LED1.anode, Part1.D13_PWM
  N3: R1.Pin_1, Part1.GND
