# Fritzing sketch B3_Blink2017 (saved by Fritzing 0.9.3b)
breadboards: 1

parts:
  Part1 = Arduino Mega 2560 (Rev3)
  LED2 = LED - 5mm [color="Green (565nm)" package="5 mm [THT]"]
  R2 = Resistor [tolerance=±1% resistance=220 package=THT]

nets:
  N1: Part1.D13_PWM, R2.Pin_0
  N2: Part1.GND, LED2.cathode
  N3: LED2.anode, R2.Pin_1
