# Fritzing sketch B3_BlinkBumpLightIR2017_MotorShield (saved by Fritzing 0.9.3b)
breadboards: 1

parts:
  TCRT5000L1 = TCRT5000L [package="DIP (Dual Inline) [THT]"]
  R12 = Resistor [tolerance=±1% resistance=220 package=THT]
  R13 = Resistor [tolerance=±1% resistance=10k package=THT]
  R14 = Resistor [tolerance=±1% resistance=10k package=THT]
  R15 = Resistor [tolerance=±1% resistance=220 package=THT]
  TCRT5000L2 = TCRT5000L [package="DIP (Dual Inline) [THT]"]
  R9 = Resistor [tolerance=±1% resistance=1k package=THT]
  S1 = SPST Switch [package=switch-spdt_kit]
  R2 = Resistor [tolerance=±1% resistance=220 package=THT]
  LED2 = LED - 5mm [color="Red (633nm)" package="5 mm [THT]"]
  R11 = PHOTOCELL [package=photocell-kit]
  R10 = PHOTOCELL [package=photocell-kit]
  R1 = Resistor [tolerance=±1% resistance=220 package=THT]
  LED1 = LED - 5mm [color="Blue (470nm)" package="5 mm [THT]"]
  R8 = Resistor [tolerance=±1% resistance=1k package=THT]
  Part1 = Arduino Mega 2560 (Rev3)
  R16 = Resistor [tolerance=±1% resistance=220 package=THT]
  LED3 = LED - 5mm [color="Green (565nm)" package="5 mm [THT]"]
  S2 = SPST Switch [package=switch-spdt_kit]
  Part2 = Arduino Motor Shield (Rev3)  # not connected
  Part3 = Arduino Prototyping Shield  # not connected

nets:
  N1: TCRT5000L1.pin1, R12.Pin_0, Part1.D42
  N2: TCRT5000L1.pin2, R13.Pin_0, Part1.A10
  N3: TCRT5000L1.pin3, R12.Pin_1
  N4: TCRT5000L1.pin4, R13.Pin_1, R14.Pin_1, TCRT5000L2.pin4, R9.Pin_1, S1.P, S1.S, R8.Pin_1, Part1.GND, LED3.cathode, S2.P
  N5: R14.Pin_0, TCRT5000L2.pin2, Part1.A11
  N6: R15.Pin_0, TCRT5000L2.pin1, Part1.D43
  N7: R15.Pin_1, TCRT5000L2.pin3
  N8: R9.Pin_0, R11.P$1, Part1.A15
  N9: S1.O, R2.Pin_1, Part1.D47
  N10: R2.Pin_0, LED2.cathode
  N11: LED2.anode, R11.P$2, R10.P$1, LED1.cathode, Part1.5V
  N12: R10.P$2, R8.Pin_0, Part1.A14
  N13: R1.Pin_0, Part1.D46, S2.O
  N14: R1.Pin_1, LED1.anode
  N15: Part1.D13_PWM, R16.Pin_0
  N16: R16.Pin_1, LED3.anode

notes:
  IR Light sensor wiring is shown as if looking down on the back of the sensors, i.e. as they are mounted.

custom parts:
  TCRT5000L: Infrared relfected light sensor.
