# Fritzing sketch B3_BlinkBumpLight_FULL_Breadboard (saved by Fritzing 0.9.3b)
breadboards: 1

parts:
  R9 = Resistor [tolerance=±1% resistance=1k package=THT]
  S1 = SPST Switch [package=switch-spdt_kit]
  R2 = Resistor [tolerance=±1% resistance=220 package=THT]
  LED2 = LED - 5mm [color="Red (633nm)" package="5 mm [THT]"]
  R11 = PHOTOCELL [package=photocell-kit]
  R10 = PHOTOCELL [package=photocell-kit]
  R1 = Resistor [tolerance=±1% resistance=220 package=THT]
  LED1 = LED - 5mm [color="Blue (470nm)" package="5 mm [THT]"]
  R8 = Resistor [tolerance=±1% resistance=1k package=THT]
  Part1 = Arduino Mega 2560 (Rev3)
  R16 = Resistor [tolerance=±1% resistance=220 package=THT]
  LED3 = LED - 5mm [color="Green (565nm)" package="5 mm [THT]"]
  S2 = SPST Switch [package=switch-spdt_kit]

nets:
  N1: R9.Pin_1, S1.P, S1.S, R8.Pin_1, Part1.GND, LED3.cathode, S2.P
  N2: S1.O, R2.Pin_1, Part1.D47
  N3: R2.Pin_0, LED2.cathode
  N4: LED2.anode, R11.P$2, R10.P$1, LED1.cathode, Part1.5V
  N5: R11.P$1, Part1.A15
  N6: R10.P$2, R8.Pin_0, Part1.A14
  N7: R1.Pin_0, Part1.D46, S2.O
  N8: R1.Pin_1, LED1.anode
  N9: Part1.D13_PWM, R16.Pin_0
  N10: R16.Pin_1, LED3.anode
