# Fritzing sketch B3_BlinkBump_FULL_Breadboard (saved by Fritzing 0.9.3b)
breadboards: 1

parts:
  S1 = SPST Switch [package=switch-spdt_kit]
  R2 = Resistor [tolerance=±1% resistance=220 package=THT]
  LED2 = LED - 5mm [color="Red (633nm)" package="5 mm [THT]"]
  R1 = Resistor [tolerance=±1% resistance=220 package=THT]
  LED1 = LED - 5mm [color="Blue (470nm)" package="5 mm [THT]"]
  Part1 = Arduino Mega 2560 (Rev3)
  R16 = Resistor [tolerance=±1% resistance=220 package=THT]
  LED3 = LED - 5mm [color="Green (565nm)" package="5 mm [THT]"]
  S2 = SPST Switch [package=switch-spdt_kit]

nets:
  N1: S1.O, R2.Pin_1, Part1.D47
  N2: S1.P, S1.S, Part1.GND, LED3.cathode, S2.P
  N3: R2.Pin_0, LED2.cathode
  N4: LED2.anode, LED1.cathode, Part1.5V
  N5: R1.Pin_0, Part1.D46, S2.O
  N6: R1.Pin_1, LED1.anode
  N7: Part1.D13_PWM, R16.Pin_0
  N8: R16.Pin_1, LED3.anode
