# Fritzing sketch B3_BlinkLight2017 (saved by Fritzing 0.9.3b)
breadboards: 1

parts:
  R9 = Resistor [tolerance=±1% resistance=1k package=THT]
  R11 = PHOTOCELL [package=photocell-kit]
  R10 = PHOTOCELL [package=photocell-kit]
  R8 = Resistor [tolerance=±1% resistance=1k package=THT]
  Part1 = Arduino Mega 2560 (Rev3)
  R16 = Resistor [tolerance=±1% resistance=220 package=THT]
  LED3 = LED - 5mm [color="Green (565nm)" package="5 mm [THT]"]

nets:
  N1: R9.Pin_0, R11.P$1, Part1.A15
  N2: R9.Pin_1, R8.Pin_1, Part1.GND, LED3.cathode
  N3: R11.P$2, R10.P$1, Part1.5V
  N4: R10.P$2, R8.Pin_0, Part1.A14
  N5: R16.Pin_1, LED3.anode
