# Fritzing sketch B3_Blink_FULL_Breadboard (saved by Fritzing 0.9.3b)
breadboards: 1

parts:
  Part1 = Arduino Mega 2560 (Rev3)
  R16 = Resistor [tolerance=±1% resistance=220 package=THT]
  LED3 = LED - 5mm [color="Green (565nm)" package="5 mm [THT]"]

nets:
  N1: Part1.GND, LED3.cathode
  N2: Part1.D13_PWM, R16.Pin_0
  N3: R16.Pin_1, LED3.anode
