# Fritzing sketch B3_BumpBlink (saved by Fritzing 0.8.5b)
breadboards: 1

parts:
  Part1 = Arduino Mega 2560 (Rev3)
  LED1 = LED - 5mm [color="Green (565nm)" package="5 mm [THT]"]
  S1 = SPST Switch [package=switch-spdt_kit]
  S2 = SPST Switch [package=switch-spdt_kit]
  R1 = Resistor [tolerance=±1% resistance=330 package=THT]
  LED2 = LED - 5mm [color="Red (633nm)" package="5 mm [THT]"]
  R2 = Resistor [tolerance=±1% resistance=330 package=THT]

nets:
  N1: Part1.5V, LED1.anode, LED2.anode
  N2: Part1.D46, S2.O, R1.Pin_0
  N3: Part1.D47, S1.O, R2.Pin_1
  N4: Part1.GND, S1.P, S2.P
  N5: LED1.cathode, R1.Pin_1
  N6: LED2.cathode, R2.Pin_0
