# Fritzing sketch B3_BumpBlink2016 (saved by Fritzing 0.9.3b)
breadboards: 1

parts:
  Part1 = Arduino Mega 2560 (Rev3)
  S3 = SPST Switch [package=switch-spdt_kit]
  S4 = SPST Switch [package=switch-spdt_kit]
  LED3 = LED - 5mm [color="Green (565nm)" package="5 mm [THT]"]
  R3 = Resistor [tolerance=±1% resistance=330 package=THT]
  R4 = Resistor [tolerance=±1% resistance=330 package=THT]
  LED4 = LED - 5mm [color="Red (633nm)" package="5 mm [THT]"]

nets:
  N1: Part1.GND, S3.P, S4.P
  N2: Part1.5V, LED3.anode, LED4.anode
  N3: Part1.D46, R4.Pin_1
  N4: Part1.D47, S4.O, R3.Pin_0
  N5: LED3.cathode, R4.Pin_0
  N6: R3.Pin_1, LED4.cathode
