# Fritzing sketch B3_BumpBlinkLightIR2016B2 (saved by Fritzing 0.9.3b)
breadboards: 1

parts:
  R12 = Resistor [tolerance=±1% resistance=220 package=THT]
  R13 = Resistor [tolerance=±1% resistance=10k package=THT]
  R14 = Resistor [tolerance=±1% resistance=10k package=THT]
  R15 = Resistor [tolerance=±1% resistance=220 package=THT]
  R9 = Resistor [tolerance=±1% resistance=10k package=THT]
  S1 = SPST Switch [package=switch-spdt_kit]
  R2 = Resistor [tolerance=±1% resistance=220 package=THT]
  LED2 = LED - 5mm [color="Red (633nm)" package="5 mm [THT]"]
  R11 = PHOTOCELL [package=photocell-kit]
  S2 = SPST Switch [package=switch-spdt_kit]
  R10 = PHOTOCELL [package=photocell-kit]
  R1 = Resistor [tolerance=±1% resistance=220 package=THT]
  LED1 = LED - 5mm [color="Green (565nm)" package="5 mm [THT]"]
  R8 = Resistor [tolerance=±1% resistance=10k package=THT]
  Part1 = Arduino Mega 2560 (Rev3)

nets:
  N1: R12.Pin_0, Part1.D42
  N2: R13.Pin_0, Part1.A10
  N3: R13.Pin_1, R14.Pin_1, R9.Pin_0, S1.P, S1.S, S2.P, R8.Pin_0, Part1.GND
  N4: R14.Pin_0, Part1.A11
  N5: R15.Pin_0, Part1.D43
  N6: R9.Pin_1, R11.P$1, Part1.A15
  N7: S1.O, R2.Pin_1, Part1.D47
  N8: R2.Pin_0, LED2.cathode
  N9: LED2.anode, R11.P$2, R10.P$1, LED1.anode, Part1.5V
  N10: S2.O, R1.Pin_0, Part1.D46
  N11: R10.P$2, R8.Pin_1, Part1.A14
  N12: R1.Pin_1, LED1.cathode
