# Fritzing sketch B3_BumpBlinkLightSonicIR (saved by Fritzing 0.8.5b)
breadboards: 1

parts:
  Part1 = Arduino Mega 2560 (Rev3)
  TCRT5000L1 = TCRT5000L [package="DIP (Dual Inline) [THT]"]
  R12 = Resistor [tolerance=±1% resistance=220 package=THT]
  R13 = Resistor [tolerance=±1% resistance=20k package=THT]
  R14 = Resistor [tolerance=±1% resistance=20k package=THT]
  R15 = Resistor [tolerance=±1% resistance=220 package=THT]
  TCRT5000L2 = TCRT5000L [package="DIP (Dual Inline) [THT]"]
  R9 = Resistor [tolerance=±1% resistance=5.1k package=THT]
  S1 = SPST Switch [package=switch-spdt_kit]
  R2 = Resistor [tolerance=±1% resistance=330 package=THT]
  LED2 = LED - 5mm [color="Red (633nm)" package="5 mm [THT]"]
  R11 = PHOTOCELL [package=photocell-kit]
  Part3 = SRF05 Ultrasonic Rangefinder
  S2 = SPST Switch [package=switch-spdt_kit]
  R10 = PHOTOCELL [package=photocell-kit]
  R1 = Resistor [tolerance=±1% resistance=330 package=THT]
  LED1 = LED - 5mm [color="Green (565nm)" package="5 mm [THT]"]
  R8 = Resistor [tolerance=±1% resistance=5.1k package=THT]

nets:
  N1: Part1.A10, TCRT5000L1.pin2, R13.Pin_0
  N2: Part1.A11, R14.Pin_0, TCRT5000L2.pin2
  N3: Part1.A14, R10.P$2, R8.Pin_1
  N4: Part1.A15, R9.Pin_1, R11.P$1
  5V: Part1.5V, LED2.anode, R11.P$2, Part3.VCC, R10.P$1, LED1.anode
  N5: Part1.D42, TCRT5000L1.pin1, R12.Pin_0
  N6: Part1.D43, R15.Pin_0, TCRT5000L2.pin1
  N7: Part1.D46, S2.O, R1.Pin_0
  N8: Part1.D47, S1.O, R2.Pin_1
  N9: Part1.D50, Part3.Trig
  N10: Part1.D51, Part3.Echo
  GND: Part1.GND, TCRT5000L1.pin4, R13.Pin_1, R14.Pin_1, TCRT5000L2.pin4, R9.Pin_0, S1.P, Part3.GND, S2.P, R8.Pin_0
  N11: TCRT5000L1.pin3, R12.Pin_1
  N12: R15.Pin_1, TCRT5000L2.pin3
  N13: R2.Pin_0, LED2.cathode
  N14: R1.Pin_1, LED1.cathode

custom parts:
  TCRT5000L: Infrared relfected light sensor.
