# Fritzing sketch B3_BumpBlinkLightSonicIR2016B (saved by Fritzing 0.9.3b)
breadboards: 1

parts:
  TCRT5000L1 = TCRT5000L [package="DIP (Dual Inline) [THT]"]
  R12 = Resistor [tolerance=±1% resistance=220 package=THT]
  R13 = Resistor [tolerance=±1% resistance=10k package=THT]
  R14 = Resistor [tolerance=±1% resistance=10k package=THT]
  R15 = Resistor [tolerance=±1% resistance=220 package=THT]
  TCRT5000L2 = TCRT5000L [package="DIP (Dual Inline) [THT]"]
  R9 = Resistor [tolerance=±1% resistance=10k package=THT]
  S1 = SPST Switch [package=switch-spdt_kit]
  R2 = Resistor [tolerance=±1% resistance=220 package=THT]
  LED2 = LED - 5mm [color="Red (633nm)" package="5 mm [THT]"]
  R11 = PHOTOCELL [package=photocell-kit]
  S2 = SPST Switch [package=switch-spdt_kit]
  R10 = PHOTOCELL [package=photocell-kit]
  R1 = Resistor [tolerance=±1% resistance=220 package=THT]
  LED1 = LED - 5mm [color="Green (565nm)" package="5 mm [THT]"]
  R8 = Resistor [tolerance=±1% resistance=10k package=THT]
  Part1 = Arduino Mega 2560 (Rev3)

nets:
  N1: TCRT5000L1.pin1, R12.Pin_0, Part1.D42
  N2: TCRT5000L1.pin2, R13.Pin_0, Part1.A10
  N3: TCRT5000L1.pin3, R12.Pin_1
  N4: TCRT5000L1.pin4, R13.Pin_1, R14.Pin_1, TCRT5000L2.pin4, R9.Pin_0, S1.P, S1.S, S2.P, R8.Pin_0, Part1.GND
  N5: R14.Pin_0, TCRT5000L2.pin2, Part1.A11
  N6: R15.Pin_0, TCRT5000L2.pin1, Part1.D43
  N7: R15.Pin_1, TCRT5000L2.pin3
  N8: R9.Pin_1, R11.P$1, Part1.A15
  N9: S1.O, R2.Pin_1, Part1.D47
  N10: R2.Pin_0, LED2.cathode
  N11: LED2.anode, R11.P$2, R10.P$1, LED1.anode, Part1.5V
  N12: S2.O, R1.Pin_0, Part1.D46
  N13: R10.P$2, R8.Pin_1, Part1.A14
  N14: R1.Pin_1, LED1.cathode

custom parts:
  TCRT5000L: Infrared relfected light sensor.
