# Fritzing sketch B3_BumpBlinkLightSonicIRServos2018 (saved by Fritzing 0.9.3b)
breadboards: 1

parts:
  TCRT5000L1 = TCRT5000L [package="DIP (Dual Inline) [THT]"]
  R12 = Resistor [tolerance=±1% resistance=220 package=THT]
  R13 = Resistor [tolerance=±1% resistance=10k package=THT]
  R14 = Resistor [tolerance=±1% resistance=10k package=THT]
  R15 = Resistor [tolerance=±1% resistance=220 package=THT]
  TCRT5000L2 = TCRT5000L [package="DIP (Dual Inline) [THT]"]
  R9 = Resistor [tolerance=±1% resistance=1k package=THT]
  S1 = SPST Switch [package=switch-spdt_kit]
  R2 = Resistor [tolerance=±1% resistance=220 package=THT]
  LED2 = LED - 5mm [color="Red (633nm)" package="5 mm [THT]"]
  R11 = PHOTOCELL [package=photocell-kit]
  Part3 = SRF05 Ultrasonic Rangefinder
  R10 = PHOTOCELL [package=photocell-kit]
  R1 = Resistor [tolerance=±1% resistance=220 package=THT]
  R8 = Resistor [tolerance=±1% resistance=1k package=THT]
  Part1 = Arduino Mega 2560 (Rev3)
  J1 = Basic Servo [part_number="Pan Servo, S2"]
  J2 = Basic Servo [part_number="Tilt Servo, S1"]
  R16 = Resistor [tolerance=±1% resistance=220 package=THT]
  LED3 = LED - 5mm [color="Green (565nm)" package="5 mm [THT]"]
  S2 = SPST Switch [package=switch-spdt_kit]
  LED4 = LED - 5mm [color="Blue (470nm)" package="5 mm [THT]"]

nets (from the breadboard view):
  N1: TCRT5000L1.pin1, R12.Pin_0, Part1.D42
  N2: TCRT5000L1.pin2, R13.Pin_0, Part1.A10
  N3: TCRT5000L1.pin3, R12.Pin_1
  VCC: TCRT5000L1.pin4, R13.Pin_1, LED2.anode, R11.P$2, Part3.VCC, R10.P$1, Part1.5V, LED4.anode
  N4: R14.Pin_0, TCRT5000L2.pin2, Part1.A11
  GND: R14.Pin_1, TCRT5000L2.pin4, R9.Pin_1, S1.P, S1.S, Part3.GND, R8.Pin_1, Part1.GND, LED3.cathode, S2.P
  N5: R15.Pin_0, TCRT5000L2.pin1, Part1.D43
  N6: R15.Pin_1, TCRT5000L2.pin3
  N7: R9.Pin_0, R11.P$1, Part1.A15
  N8: S1.O, R2.Pin_1, Part1.D47
  N9: R2.Pin_0, LED2.cathode
  N10: Part3.Trig, Part1.D51
  N11: Part3.Echo, Part1.D50
  N12: R10.P$2, R8.Pin_0, Part1.A14
  N13: R1.Pin_0, Part1.D46, S2.O
  N14: R1.Pin_1, LED4.cathode
  N15: Part1.D13_PWM, R16.Pin_0
  N16: Part1.D10_PWM, J2.pulse
  N17: Part1.D9_PWM, J1.pulse
  N18: R16.Pin_1, LED3.anode

notes:
  IR Light sensor wiring is shown as if looking down on the back of the sensors, i.e. as they are mounted.

custom parts:
  TCRT5000L: Infrared relfected light sensor.
