# Fritzing sketch B3_BumpBlinkbackup (saved by Fritzing 0.9.3b)
breadboards: 1

parts:
  LED1 = LED - 5mm [color="Green (565nm)" package="5 mm [THT]"]
  S1 = SPST Switch [package=switch-spdt_kit]
  S2 = SPST Switch [package=switch-spdt_kit]
  R1 = Resistor [tolerance=±1% resistance=330 package=THT]
  LED2 = LED - 5mm [color="Red (633nm)" package="5 mm [THT]"]
  R2 = Resistor [tolerance=±1% resistance=330 package=THT]
  Part1 = Arduino Mega 2560 (Rev3)

nets:
  N1: LED1.cathode, R1.Pin_1
  N2: LED1.anode, LED2.anode, Part1.5V
  N3: S1.O, R2.Pin_1, Part1.D47
  N4: S1.P, S2.P, Part1.GND
  N5: S2.O, R1.Pin_0, Part1.D46
  N6: LED2.cathode, R2.Pin_0
