# Fritzing sketch B3_BumpSonic (saved by Fritzing 0.8.5b)
breadboards: 1

parts:
  Part1 = Arduino Mega 2560 (Rev3)
  LED1 = LED - 5mm [color="Green (565nm)" package="5 mm [THT]"]
  R1 = Resistor [tolerance=±1% resistance=220 package=THT]
  S1 = SPST Switch [package=switch-spdt_kit]
  S2 = SPST Switch [package=switch-spdt_kit]
  Part2 = SRF05 Ultrasonic Rangefinder

nets:
  5V: Part1.5V, R1.Pin_0, Part2.VCC
  N1: Part1.D46, S2.O
  N2: Part1.D47, S1.O
  N3: Part1.D50, Part2.Trig
  N4: Part1.D51, Part2.Echo
  GND: Part1.GND, LED1.cathode, S1.P, S2.P, Part2.GND
  N5: LED1.anode, R1.Pin_1
