# Fritzing sketch B3_IR (saved by Fritzing 0.8.5b)
breadboards: 1

parts:
  Part1 = Arduino Mega 2560 (Rev3)
  TCRT5000L1 = TCRT5000L [package="DIP (Dual Inline) [THT]"]
  R12 = Resistor [tolerance=±1% resistance=220 package=THT]
  R13 = Resistor [tolerance=±1% resistance=20k package=THT]
  R14 = Resistor [tolerance=±1% resistance=20k package=THT]
  R15 = Resistor [tolerance=±1% resistance=220 package=THT]
  TCRT5000L2 = TCRT5000L [package="DIP (Dual Inline) [THT]"]

nets:
  N1: Part1.A10, TCRT5000L1.pin2, R13.Pin_0
  N2: Part1.A11, R14.Pin_0, TCRT5000L2.pin2
  N3: Part1.D42, TCRT5000L1.pin1, R12.Pin_0
  N4: Part1.D43, R15.Pin_0, TCRT5000L2.pin1
  N5: Part1.GND, TCRT5000L1.pin4, R13.Pin_1, R14.Pin_1, TCRT5000L2.pin4
  N6: TCRT5000L1.pin3, R12.Pin_1
  N7: R15.Pin_1, TCRT5000L2.pin3

custom parts:
  TCRT5000L: Infrared relfected light sensor.
