# Fritzing sketch B3_Light (saved by Fritzing 0.8.5b)
breadboards: 1

parts:
  Part1 = Arduino Mega 2560 (Rev3)
  LED1 = LED - 5mm [color="Green (565nm)" package="5 mm [THT]"]
  R1 = Resistor [tolerance=±1% resistance=220 package=THT]
  R2 = PHOTOCELL [package=photocell-kit]
  R3 = PHOTOCELL [package=photocell-kit]
  R4 = Resistor [tolerance=±1% resistance=6.8k package=THT]
  R5 = Resistor [tolerance=±1% resistance=6.8k package=THT]

nets:
  N1: Part1.A14, R2.P$2, R5.Pin_1
  N2: Part1.A15, R3.P$1, R4.Pin_1
  N3: Part1.5V, R1.Pin_0, R2.P$1, R3.P$2
  N4: Part1.GND, LED1.cathode, R4.Pin_0, R5.Pin_0
  N5: LED1.anode, R1.Pin_1
