# Fritzing sketch B3_Many (saved by Fritzing 0.8.5b)
breadboards: 1

parts:
  Part1 = Arduino Mega 2560 (Rev3)
  LED1 = LED - 5mm [color="Green (565nm)" package="5 mm [THT]"]
  R1 = Resistor [tolerance=±1% resistance=220 package=THT]
  S1 = SPST Switch [package=switch-spdt_kit]
  S2 = SPST Switch [package=switch-spdt_kit]
  Part2 = SRF05 Ultrasonic Rangefinder
  R2 = PHOTOCELL [package=photocell-kit]
  R3 = PHOTOCELL [package=photocell-kit]
  R4 = Resistor [tolerance=±1% resistance=6.8k package=THT]
  R5 = Resistor [tolerance=±1% resistance=6.8k package=THT]

nets:
  GND: Part1.A14, Part1.A15, Part1.GND, LED1.cathode, S1.P, S2.P, Part2.GND, R4.Pin_0, R5.Pin_0
  5V: Part1.5V, R1.Pin_0, Part2.VCC, R2.P$1, R3.P$2
  N1: Part1.D46, S2.O
  N2: Part1.D47, S1.O
  N3: Part1.D50, Part2.Trig
  N4: Part1.D51, Part2.Echo
  N5: LED1.anode, R1.Pin_1
  N6: R2.P$2, R5.Pin_1
  N7: R3.P$1, R4.Pin_1
