# Fritzing sketch B3_Sonic (saved by Fritzing 0.8.5b)
breadboards: 1

parts:
  Part1 = Arduino Mega 2560 (Rev3)
  LED1 = LED - 5mm [color="Green (565nm)" package="5 mm [THT]"]
  R1 = Resistor [tolerance=±1% resistance=220 package=THT]
  Part2 = SRF05 Ultrasonic Rangefinder

nets:
  5V: Part1.5V, R1.Pin_0, Part2.VCC
  N1: Part1.D50, Part2.Trig
  N2: Part1.D51, Part2.Echo
  GND: Part1.GND, LED1.cathode, Part2.GND
  N3: LED1.anode, R1.Pin_1
