# Fritzing sketch SimpleBumpLEDandPullUpResistor (saved by Fritzing 0.9.3b)
breadboards: 1

parts:
  R1 = Resistor [tolerance=±5% resistance=220 package=THT]
  LED1 = LED - 5mm [color="Red (633nm)" package="5 mm [THT]"]
  S1 = Toggle Switch [package=THT]
  V1 = DC Power [voltage=5]
  R2 = Resistor [tolerance=±5% resistance=220 package=THT]
  IC1 = IC, DIP package, 4 pins [chip_label=IC]

nets:
  N1: R1.Pin_0, V1.V+
  N2: R1.Pin_1, LED1.anode
  N3: LED1.cathode, S1.L2
  N4: S1.COM, V1.V-
  N5: R2.Pin_0, IC1.pin3
  5V: R2.Pin_1
